# Fritzing sketch OfficialFritzingDiagram (saved by Fritzing 1.0.3b)
breadboards: 1

parts:
  MOTOR2 = Vibration Motor
  Part6 = Adafruit BNO055 STEMMA QT [part_number="Adafruit #4646"]
  MCU1 = Raspberry Pi Zero
  J2 = Piezo Speaker
  DHT1 = DHT22 Humidity and Temperature Sensor

nets:
  N1: MOTOR2.POS, MCU1.pin_16
  GND: MOTOR2.NEG, Part6.GND, MCU1.pin_6, J2.pin1, DHT1.GND
  VCC: Part6.VCC, MCU1.pin_2, DHT1.VDD
  N2: Part6.SCL, MCU1.pin_5
  N3: Part6.SDA, MCU1.pin_3
  N4: MCU1.pin_7, DHT1.DATA

notes:
  Raspberry Pi 4B
  5V : positive rail breadboard
  GND : negative rail breadboard
  GPIO 2 : SDA BNO055
  GPIO 3 : SCL BNO055
  GPIO 4 : out DHT22
  GPIO 23 : + Vibration
  GPIO 24 : + Buzzer
  BNO055 Orientation Sensor
  VCC : positive rail breadboard
  GND : negative rail breadboard
  SCL : GPIO 3 (Raspberry Pi)
  SDA : GPIO 2 (Raspberry Pi)
  DHT22 Temperature/Humidity Sensor
  + : positive rail breadboard
  output : GPIO pin 4 (Raspberry Pi)
  - : negative rail breadboard
  Vibration Motor
  + : GPIO 23 (Raspberry Pi)
  - : negative rail breadboard
  Piezo Buzzer
  + : GPIO 24 (Raspberry Pi)
  - : negative rail breadboard

custom parts:
  Vibration Motor: An eccentric vibration motor!
  Adafruit BNO055 STEMMA QT: If you've ever ordered and wire up a 9-DOF sensor, chances are you've also realized the challenge of turning the sensor data from an accelerometer, gyroscope, and magnetometer into actual "3D space orientation"! Orientation is a hard problem to solve. The sensor fusion algorithms (the secret sauce that blends accelerometer, magnetometer, and gyroscope data into stable three-axis orientation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
